# Fritzing sketch PhysicalSchematic (saved by Fritzing 0.8.7b)
breadboards: 1

parts:
  photoresistor = Photocell (LDR) [package=THT]
  resistor = Resistor [tolerance=±5% resistance=10k package=THT]
  Arduino = Arduino Uno (Rev3)

nets:
  N1: photoresistor.pin_0, resistor.Pin_1, Arduino.A0
  N2: photoresistor.pin_1, Arduino.5V
  N3: resistor.Pin_0, Arduino.GND
